// Logisim project 7_SEGEMENT.circ as structural Verilog: 2 circuits, main circuit main
module main (
  input  a,
  input  b,
  input  c,
  input  d
);

  wire display_1_s1, display_1_s2, display_1_s3, display_1_s4, display_1_s5, display_1_s6, display_1_s7;

  DISPLAY display_1 (
    .a(a), .b(b), .c(c), .d(d), .s1(display_1_s1), .s2(display_1_s2), .s3(display_1_s3), .s4(display_1_s4),
    .s5(display_1_s5), .s6(display_1_s6), .s7(display_1_s7));
  _7_Segment_Display u_7_segment_display_1 (
    .g(display_1_s4), .f(display_1_s1), .a(display_1_s2), .b(display_1_s3), .e(display_1_s7),
    .d(display_1_s6), .c(display_1_s5));  // open: dp

  // Notes on the sheet:
  //   d: pull=down
endmodule

module DISPLAY (
  input  a,
  input  b,
  input  c,
  input  d,
  output s1,
  output s2,
  output s3,
  output s4,
  output s5,
  output s6,
  output s7
);

  wire and_1_out, and_2_out, and_3_out, and_4_out, and_5_out, and_6_out, and_7_out, and_8_out, and_9_out,
       and_10_out, and_11_out, and_12_out, and_13_out, and_14_out, and_15_out, and_16_out, and_17_out,
       and_18_out, and_19_out, and_20_out, and_21_out, and_22_out, and_23_out, not_1_out, not_2_out,
       not_3_out, not_4_out;

  not not_1 (not_1_out, a);
  not not_2 (not_2_out, b);
  not not_3 (not_3_out, c);
  not not_4 (not_4_out, d);
  and and_1 (and_1_out, not_3_out, not_4_out);
  and and_2 (and_2_out, b, not_3_out);
  and and_3 (and_3_out, b, not_4_out);
  and and_4 (and_4_out, not_2_out, not_4_out);
  and and_5 (and_5_out, b, d);
  and and_6 (and_6_out, not_1_out, not_2_out);
  and and_7 (and_7_out, not_1_out, not_3_out, not_4_out);
  and and_8 (and_8_out, not_2_out, not_3_out);
  and and_9 (and_9_out, not_1_out, c, d);
  and and_10 (and_10_out, not_2_out, c);
  and and_11 (and_11_out, b, not_3_out);
  and and_12 (and_12_out, c, not_4_out);
  and and_13 (and_13_out, not_1_out, d);
  and and_14 (and_14_out, not_2_out, not_3_out);
  and and_15 (and_15_out, not_1_out, b);
  and and_16 (and_16_out, not_2_out, not_4_out);
  and and_17 (and_17_out, not_2_out, c);
  and and_18 (and_18_out, b, not_3_out, d);
  and and_19 (and_19_out, c, not_4_out);
  and and_20 (and_20_out, not_2_out, not_4_out);
  and and_21 (and_21_out, c, not_4_out);
  and and_22 (and_22_out, a, c);
  and and_23 (and_23_out, a, b);
  or or_1 (s1, and_1_out, and_2_out, and_3_out, a);
  or or_2 (s2, and_4_out, c, and_5_out, a);
  or or_3 (s3, and_6_out, and_7_out, and_8_out, and_9_out);
  or or_4 (s4, and_10_out, and_11_out, a, and_12_out);
  or or_5 (s5, and_13_out, and_14_out, and_15_out);
  or or_6 (s6, and_16_out, and_17_out, and_18_out, and_19_out, a);
  or or_7 (s7, and_20_out, and_21_out, and_22_out, and_23_out);
endmodule
