// Logisim project ALU_.circ as structural Verilog
module main (
  input  [3:0] op,
  input  [31:0] a,
  input  [31:0] b,
  output zero,
  output [31:0] result,
  output overflow
);

  therty_two_bit_alu therty_two_bit_alu_1 (
    .Operation(op), .a(a), .b(b), .Zero(zero), .result(result), .Overflow(overflow));

  // Notes on the sheet:
  //   AND => 0000
  //   OR => 0001
  //   ADD => 0010
  //   SUB => 0110
  //   SLT => 0011
  //   NOR => 0100
  //   Inputs and outputs are on hexidecimal
  //   @Copy right,  Student.Ahmed Fouatih Hamza Faiz
  //        winter-2025   ARCHI-2
endmodule

module one_bit_adder (
  input  a,
  input  b,
  input  carry_in,
  output sum,
  output carry_out
);

  wire and_1_out, and_2_out, and_3_out, and_4_out, and_5_out, and_6_out, and_7_out, not_1_out, not_2_out,
       not_3_out;

  not not_1 (not_1_out, a);
  not not_2 (not_2_out, b);
  not not_3 (not_3_out, carry_in);
  and and_1 (and_1_out, not_1_out, not_2_out, carry_in);
  and and_2 (and_2_out, not_1_out, b, not_3_out);
  and and_3 (and_3_out, a, not_2_out, not_3_out);
  and and_4 (and_4_out, a, b, carry_in);
  and and_5 (and_5_out, b, carry_in);
  and and_6 (and_6_out, a, carry_in);
  and and_7 (and_7_out, a, b);
  or or_1 (sum, and_1_out, and_2_out, and_3_out, and_4_out);
  or or_2 (carry_out, and_5_out, and_6_out, and_7_out);
endmodule

module one_bit_alu (
  input  Ainvert,
  input  Binvert,
  input  Carry_in,
  input  [3:0] Operation,
  input  a,
  input  b,
  input  Less,
  output Result,
  output Set,
  output Overflow
);

  wire and_1_out, multiplexer_1_out, multiplexer_2_out, not_1_out, not_2_out, one_bit_adder_1_sum, or_1_out;

  not not_1 (not_1_out, a);
  not not_2 (not_2_out, b);
  Multiplexer multiplexer_1 (.in0(a), .in1(not_1_out), .out(multiplexer_1_out), .sel(Ainvert));
  Multiplexer multiplexer_2 (.in0(b), .in1(not_2_out), .out(multiplexer_2_out), .sel(Binvert));
  and and_1 (and_1_out, multiplexer_1_out, multiplexer_2_out);
  or or_1 (or_1_out, multiplexer_1_out, multiplexer_2_out);
  one_bit_adder one_bit_adder_1 (
    .a(multiplexer_1_out), .b(multiplexer_2_out), .carry_in(Carry_in), .sum(one_bit_adder_1_sum),
    .carry_out(Set));
  overflow_detect overflow_detect_1 (.a(multiplexer_1_out), .b(multiplexer_2_out), .cin(Set), .overflow(Overflow));
  Multiplexer #(.select(4)) multiplexer_3 (
    .in0(and_1_out), .in1(or_1_out), .in2(one_bit_adder_1_sum), .in3(Less), .in4(and_1_out),
    .in6(one_bit_adder_1_sum), .out(Result), .sel(Operation));  // open: in5, in7, in8, in9, in10, in11, in12, in13, in14, in15
endmodule

module therty_two_bit_alu (
  input  [3:0] Operation,
  input  [31:0] a,
  input  [31:0] b,
  output Zero,
  output [31:0] result,
  output Overflow
);

  wire Ainvert, Binvert, Carry_in, Less, one_bit_alu_1_set, one_bit_alu_2_set, one_bit_alu_3_set,
       one_bit_alu_4_set, one_bit_alu_5_set, one_bit_alu_6_set, one_bit_alu_7_set, one_bit_alu_8_set,
       one_bit_alu_9_set, one_bit_alu_10_set, one_bit_alu_11_set, one_bit_alu_12_set, one_bit_alu_13_set,
       one_bit_alu_14_set, one_bit_alu_15_set, one_bit_alu_16_set, one_bit_alu_17_set, one_bit_alu_18_set,
       one_bit_alu_19_set, one_bit_alu_20_set, one_bit_alu_21_set, one_bit_alu_22_set, one_bit_alu_23_set,
       one_bit_alu_24_set, one_bit_alu_25_set, one_bit_alu_26_set, one_bit_alu_27_set, one_bit_alu_28_set,
       one_bit_alu_29_set, one_bit_alu_30_set, one_bit_alu_31_set, one_bit_alu_32_set, or_1_out, or_2_out;
  wire [3:0] Operation_t;

  Option_menu_handler option_menu_handler_1 (
    .a3(Operation[3]), .a2(Operation[2]), .a1(Operation[1]), .a0(Operation[0]), .Ainverter(Ainvert),
    .Binverter(Binvert), .Carry_in(Carry_in), .op0(Operation_t[0]), .op1(Operation_t[1]),
    .op2(Operation_t[2]), .op3(Operation_t[3]));
  one_bit_alu one_bit_alu_1 (
    .Ainvert(Ainvert), .Binvert(Binvert), .Carry_in(Carry_in), .Operation(Operation_t), .a(a[0]), .b(b[0]),
    .Less(Less), .Result(result[0]), .Set(one_bit_alu_1_set));  // open: Overflow
  one_bit_alu one_bit_alu_2 (
    .Ainvert(Ainvert), .Binvert(Binvert), .Carry_in(one_bit_alu_1_set), .Operation(Operation_t), .a(a[1]),
    .b(b[1]), .Less(1'b0), .Result(result[1]), .Set(one_bit_alu_2_set));  // open: Overflow
  one_bit_alu one_bit_alu_3 (
    .Ainvert(Ainvert), .Binvert(Binvert), .Carry_in(one_bit_alu_2_set), .Operation(Operation_t), .a(a[2]),
    .b(b[2]), .Less(1'b0), .Result(result[2]), .Set(one_bit_alu_3_set));  // open: Overflow
  one_bit_alu one_bit_alu_4 (
    .Ainvert(Ainvert), .Binvert(Binvert), .Carry_in(one_bit_alu_3_set), .Operation(Operation_t), .a(a[3]),
    .b(b[3]), .Less(1'b0), .Result(result[3]), .Set(one_bit_alu_4_set));  // open: Overflow
  one_bit_alu one_bit_alu_5 (
    .Ainvert(Ainvert), .Binvert(Binvert), .Carry_in(one_bit_alu_4_set), .Operation(Operation_t), .a(a[4]),
    .b(b[4]), .Less(1'b0), .Result(result[4]), .Set(one_bit_alu_5_set));  // open: Overflow
  one_bit_alu one_bit_alu_6 (
    .Ainvert(Ainvert), .Binvert(Binvert), .Carry_in(one_bit_alu_5_set), .Operation(Operation_t), .a(a[5]),
    .b(b[5]), .Less(1'b0), .Result(result[5]), .Set(one_bit_alu_6_set));  // open: Overflow
  one_bit_alu one_bit_alu_7 (
    .Ainvert(Ainvert), .Binvert(Binvert), .Carry_in(one_bit_alu_6_set), .Operation(Operation_t), .a(a[6]),
    .b(b[6]), .Less(1'b0), .Result(result[6]), .Set(one_bit_alu_7_set));  // open: Overflow
  one_bit_alu one_bit_alu_8 (
    .Ainvert(Ainvert), .Binvert(Binvert), .Carry_in(one_bit_alu_7_set), .Operation(Operation_t), .a(a[7]),
    .b(b[7]), .Less(1'b0), .Result(result[7]), .Set(one_bit_alu_8_set));  // open: Overflow
  one_bit_alu one_bit_alu_9 (
    .Ainvert(Ainvert), .Binvert(Binvert), .Carry_in(one_bit_alu_8_set), .Operation(Operation_t), .a(a[8]),
    .b(b[8]), .Less(1'b0), .Result(result[8]), .Set(one_bit_alu_9_set));  // open: Overflow
  one_bit_alu one_bit_alu_10 (
    .Ainvert(Ainvert), .Binvert(Binvert), .Carry_in(one_bit_alu_9_set), .Operation(Operation_t), .a(a[9]),
    .b(b[9]), .Less(1'b0), .Result(result[9]), .Set(one_bit_alu_10_set));  // open: Overflow
  one_bit_alu one_bit_alu_11 (
    .Ainvert(Ainvert), .Binvert(Binvert), .Carry_in(one_bit_alu_10_set), .Operation(Operation_t), .a(a[10]),
    .b(b[10]), .Less(1'b0), .Result(result[10]), .Set(one_bit_alu_11_set));  // open: Overflow
  one_bit_alu one_bit_alu_12 (
    .Ainvert(Ainvert), .Binvert(Binvert), .Carry_in(one_bit_alu_11_set), .Operation(Operation_t), .a(a[11]),
    .b(b[11]), .Less(1'b0), .Result(result[11]), .Set(one_bit_alu_12_set));  // open: Overflow
  one_bit_alu one_bit_alu_13 (
    .Ainvert(Ainvert), .Binvert(Binvert), .Carry_in(one_bit_alu_12_set), .Operation(Operation_t), .a(a[12]),
    .b(b[12]), .Less(1'b0), .Result(result[12]), .Set(one_bit_alu_13_set));  // open: Overflow
  one_bit_alu one_bit_alu_14 (
    .Ainvert(Ainvert), .Binvert(Binvert), .Carry_in(one_bit_alu_13_set), .Operation(Operation_t), .a(a[13]),
    .b(b[13]), .Less(1'b0), .Result(result[13]), .Set(one_bit_alu_14_set));  // open: Overflow
  one_bit_alu one_bit_alu_15 (
    .Ainvert(Ainvert), .Binvert(Binvert), .Carry_in(one_bit_alu_14_set), .Operation(Operation_t), .a(a[14]),
    .b(b[14]), .Less(1'b0), .Result(result[14]), .Set(one_bit_alu_15_set));  // open: Overflow
  one_bit_alu one_bit_alu_16 (
    .Ainvert(Ainvert), .Binvert(Binvert), .Carry_in(one_bit_alu_15_set), .Operation(Operation_t), .a(a[15]),
    .b(b[15]), .Less(1'b0), .Result(result[15]), .Set(one_bit_alu_16_set));  // open: Overflow
  one_bit_alu one_bit_alu_17 (
    .Ainvert(Ainvert), .Binvert(Binvert), .Carry_in(one_bit_alu_16_set), .Operation(Operation_t), .a(a[16]),
    .b(b[16]), .Less(1'b0), .Result(result[16]), .Set(one_bit_alu_17_set));  // open: Overflow
  one_bit_alu one_bit_alu_18 (
    .Ainvert(Ainvert), .Binvert(Binvert), .Carry_in(one_bit_alu_17_set), .Operation(Operation_t), .a(a[17]),
    .b(b[17]), .Less(1'b0), .Result(result[17]), .Set(one_bit_alu_18_set));  // open: Overflow
  one_bit_alu one_bit_alu_19 (
    .Ainvert(Ainvert), .Binvert(Binvert), .Carry_in(one_bit_alu_18_set), .Operation(Operation_t), .a(a[18]),
    .b(b[18]), .Less(1'b0), .Result(result[18]), .Set(one_bit_alu_19_set));  // open: Overflow
  one_bit_alu one_bit_alu_20 (
    .Ainvert(Ainvert), .Binvert(Binvert), .Carry_in(one_bit_alu_19_set), .Operation(Operation_t), .a(a[19]),
    .b(b[19]), .Less(1'b0), .Result(result[19]), .Set(one_bit_alu_20_set));  // open: Overflow
  one_bit_alu one_bit_alu_21 (
    .Ainvert(Ainvert), .Binvert(Binvert), .Carry_in(one_bit_alu_20_set), .Operation(Operation_t), .a(a[20]),
    .b(b[20]), .Less(1'b0), .Result(result[20]), .Set(one_bit_alu_21_set));  // open: Overflow
  one_bit_alu one_bit_alu_22 (
    .Ainvert(Ainvert), .Binvert(Binvert), .Carry_in(one_bit_alu_21_set), .Operation(Operation_t), .a(a[21]),
    .b(b[21]), .Less(1'b0), .Result(result[21]), .Set(one_bit_alu_22_set));  // open: Overflow
  one_bit_alu one_bit_alu_23 (
    .Ainvert(Ainvert), .Binvert(Binvert), .Carry_in(one_bit_alu_22_set), .Operation(Operation_t), .a(a[22]),
    .b(b[22]), .Less(1'b0), .Result(result[22]), .Set(one_bit_alu_23_set));  // open: Overflow
  one_bit_alu one_bit_alu_24 (
    .Ainvert(Ainvert), .Binvert(Binvert), .Carry_in(one_bit_alu_23_set), .Operation(Operation_t), .a(a[23]),
    .b(b[23]), .Less(1'b0), .Result(result[23]), .Set(one_bit_alu_24_set));  // open: Overflow
  one_bit_alu one_bit_alu_25 (
    .Ainvert(Ainvert), .Binvert(Binvert), .Carry_in(one_bit_alu_24_set), .Operation(Operation_t), .a(a[24]),
    .b(b[24]), .Less(1'b0), .Result(result[24]), .Set(one_bit_alu_25_set));  // open: Overflow
  one_bit_alu one_bit_alu_26 (
    .Ainvert(Ainvert), .Binvert(Binvert), .Carry_in(one_bit_alu_25_set), .Operation(Operation_t), .a(a[25]),
    .b(b[25]), .Less(1'b0), .Result(result[25]), .Set(one_bit_alu_26_set));  // open: Overflow
  one_bit_alu one_bit_alu_27 (
    .Ainvert(Ainvert), .Binvert(Binvert), .Carry_in(one_bit_alu_26_set), .Operation(Operation_t), .a(a[26]),
    .b(b[26]), .Less(1'b0), .Result(result[26]), .Set(one_bit_alu_27_set));  // open: Overflow
  one_bit_alu one_bit_alu_28 (
    .Ainvert(Ainvert), .Binvert(Binvert), .Carry_in(one_bit_alu_27_set), .Operation(Operation_t), .a(a[27]),
    .b(b[27]), .Less(1'b0), .Result(result[27]), .Set(one_bit_alu_28_set));  // open: Overflow
  one_bit_alu one_bit_alu_29 (
    .Ainvert(Ainvert), .Binvert(Binvert), .Carry_in(one_bit_alu_28_set), .Operation(Operation_t), .a(a[28]),
    .b(b[28]), .Less(1'b0), .Result(result[28]), .Set(one_bit_alu_29_set));  // open: Overflow
  one_bit_alu one_bit_alu_30 (
    .Ainvert(Ainvert), .Binvert(Binvert), .Carry_in(one_bit_alu_29_set), .Operation(Operation_t), .a(a[29]),
    .b(b[29]), .Less(1'b0), .Result(result[29]), .Set(one_bit_alu_30_set));  // open: Overflow
  one_bit_alu one_bit_alu_31 (
    .Ainvert(Ainvert), .Binvert(Binvert), .Carry_in(one_bit_alu_30_set), .Operation(Operation_t), .a(a[30]),
    .b(b[30]), .Less(1'b0), .Result(result[30]), .Set(one_bit_alu_31_set));  // open: Overflow
  one_bit_alu one_bit_alu_32 (
    .Ainvert(Ainvert), .Binvert(Binvert), .Carry_in(one_bit_alu_31_set), .Operation(Operation_t), .a(a[31]),
    .b(b[31]), .Less(1'b0), .Result(result[31]), .Set(one_bit_alu_32_set), .Overflow(Overflow));
  or or_1 (or_1_out, Overflow, one_bit_alu_32_set);
  not not_1 (Less, or_1_out);
  or or_2 (or_2_out, result[0], result[1], result[2], result[3], result[10], result[9], result[8], result[7], result[8], result[9], result[10], result[11], result[12], result[13], result[14], result[15], result[4], result[16], result[17], result[18], result[31], result[30], result[29], result[28], result[27], result[26], result[25], result[24], result[23], result[22], result[21], result[20], result[19]);
  not not_2 (Zero, or_2_out);
endmodule

module Option_menu_handler (
  input  a3,
  input  a2,
  input  a1,
  input  a0,
  output Ainverter,
  output Binverter,
  output Carry_in,
  output op0,
  output op1,
  output op2,
  output op3
);

  wire and_2_out, and_3_out, and_4_out, and_5_out, and_6_out, and_7_out, and_8_out, not_1_out, not_2_out,
       not_3_out, not_4_out;

  not not_1 (not_1_out, a3);
  not not_2 (not_2_out, a2);
  not not_3 (not_3_out, a1);
  not not_4 (not_4_out, a0);
  and and_1 (Ainverter, not_1_out, a2, not_3_out, not_4_out);
  and and_2 (and_2_out, not_1_out, not_2_out, a1, a0);
  and and_3 (and_3_out, not_1_out, a2, not_4_out);
  and and_4 (and_4_out, not_1_out, not_2_out, a1, a0);
  and and_5 (and_5_out, not_1_out, a2, a1, not_4_out);
  and and_6 (and_6_out, a2, not_3_out);
  and and_7 (and_7_out, a2, a0);
  and and_8 (and_8_out, a3, a2);
  or or_1 (Binverter, and_2_out, and_3_out);
  or or_2 (Carry_in, and_4_out, and_5_out);
  or or_3 (op2, and_6_out, and_7_out, and_8_out);

  assign op0 = a0;
  assign op1 = a1;
  assign op3 = a3;
endmodule

module overflow_detect (
  input  a,
  input  b,
  input  cin,
  output overflow
);

  wire and_1_out, and_2_out, and_3_out;

  and and_1 (and_1_out, b, cin);
  and and_2 (and_2_out, a, cin);
  and and_3 (and_3_out, a, b);
  or or_1 (overflow, and_1_out, and_2_out, and_3_out);
endmodule
