// Logisim project Challenge2.circ as structural Verilog
module main (
  input  Clk,
  output Overflow_FLAG
);

  wire For_Branche_out, maincontrol_1_aluop0, maincontrol_1_aluop1, maincontrol_1_alusrc,
       maincontrol_1_branch, maincontrol_1_memotoreg, maincontrol_1_memread, maincontrol_1_memwrite,
       maincontrol_1_regdst, maincontrol_1_regfwrite, therty_two_bit_alu_1_zero;
  wire [1:1] undriven;
  wire [3:0] alucontrol_1_operation;
  wire [31:0] adder_1_out, adder_2_out, Data_MEM_dout, fileregister_1_data1, fileregister_1_data2,
       immgen_1_out_2, multiplexer_1_out, multiplexer_2_out, multiplexer_3_out, pc_1_out_3, ram_1_dout,
       therty_two_bit_alu_1_result;

  PC pc_1 (.Clk(Clk), .in_2(multiplexer_2_out), .out_3(pc_1_out_3));
  RAM #(.dataWidth(32)) ram_1 (.din(multiplexer_2_out), .dout(ram_1_dout));  // open: addr, we, oe, clk
  Adder #(.width(32)) adder_1 (.a(32'h4), .b(pc_1_out_3), .out(adder_1_out));  // open: cin, cout
  MainControl maincontrol_1 (
    .op5(ram_1_dout[5]), .op4(ram_1_dout[4]), .op3(ram_1_dout[3]), .op2(ram_1_dout[2]), .op1(ram_1_dout[1]),
    .op0(ram_1_dout[0]), .RegDst(maincontrol_1_regdst), .ALUSrc(maincontrol_1_alusrc),
    .MemotoReg(maincontrol_1_memotoreg), .RegfWrite(maincontrol_1_regfwrite),
    .MemRead(maincontrol_1_memread), .MemWrite(maincontrol_1_memwrite), .Branch(maincontrol_1_branch),
    .ALUOp1(maincontrol_1_aluop1), .ALUOp0(maincontrol_1_aluop0));
  fileregister fileregister_1 (
    .WriteSignl(maincontrol_1_regfwrite), .registre1(ram_1_dout[20:16]), .registre2(ram_1_dout[25:21]),
    .regWrite(ram_1_dout[12:8]), .DataWrite(multiplexer_3_out), .data1(fileregister_1_data1),
    .data2(fileregister_1_data2));
  ImmGen immgen_1 (.imm({ram_1_dout[31:22], undriven[1], ram_1_dout[20]}), .out_2(immgen_1_out_2));
  Multiplexer #(.width(32)) multiplexer_1 (
    .in0(fileregister_1_data2), .in1(immgen_1_out_2), .out(multiplexer_1_out), .sel(maincontrol_1_alusrc));
  ALUControl alucontrol_1 (
    .ALUOp1(maincontrol_1_aluop1), .ALUOp0(maincontrol_1_aluop0), .Func3(ram_1_dout[3]),
    .Func2(ram_1_dout[2]), .Func1(ram_1_dout[1]), .Func0(ram_1_dout[0]), .Operation(alucontrol_1_operation));
  therty_two_bit_alu therty_two_bit_alu_1 (
    .Operation(alucontrol_1_operation), .a(fileregister_1_data1), .b(multiplexer_1_out),
    .Zero(therty_two_bit_alu_1_zero), .result(therty_two_bit_alu_1_result), .Overflow(Overflow_FLAG));
  Adder #(.width(32)) adder_2 (.a(pc_1_out_3), .b(immgen_1_out_2), .out(adder_2_out));  // open: cin, cout
  and For_Branche (For_Branche_out, maincontrol_1_branch, therty_two_bit_alu_1_zero);
  RAM #(.dataWidth(32)) Data_MEM (
    .oe(maincontrol_1_memread), .din(therty_two_bit_alu_1_result), .dout(Data_MEM_dout));  // open: addr, we, clk
  Multiplexer #(.width(32)) multiplexer_2 (
    .in0(adder_1_out), .in1(adder_2_out), .out(multiplexer_2_out), .sel(For_Branche_out));
  Multiplexer #(.width(32)) multiplexer_3 (
    .in0(Data_MEM_dout), .in1(therty_two_bit_alu_1_result), .out(multiplexer_3_out),
    .sel(maincontrol_1_memotoreg));

  // Notes on the sheet:
  //   Best Regards;
  //   These circuite implementa a datapath Brown for RISC-V (simple version).
  //   These circuite is developed by Student.Ahmed Fouatih Hamza Faiz,   ARCHI 2     winter-25
endmodule

module ALUControl (
  input  ALUOp1,
  input  ALUOp0,
  input  Func3,
  input  Func2,
  input  Func1,
  input  Func0,
  output [3:0] Operation
);

  wire and_1_out, not_1_out, not_2_out, not_3_out, or_1_out;

  or or_1 (or_1_out, Func3, Func0);
  and and_1 (and_1_out, ALUOp1, Func1);
  and and_2 (Operation[0], ALUOp1, or_1_out);
  and and_3 (Operation[3], ALUOp0, not_1_out);
  not not_1 (not_1_out, ALUOp0);
  or or_2 (Operation[2], ALUOp0, and_1_out);
  not not_2 (not_2_out, ALUOp1);
  or or_3 (Operation[1], not_2_out, not_3_out);
  not not_3 (not_3_out, Func2);

  // Notes on the sheet:
  //   Go to main; These is a bug in the logicim
endmodule

module MainControl (
  input  op5,
  input  op4,
  input  op3,
  input  op2,
  input  op1,
  input  op0,
  output RegDst,
  output ALUSrc,
  output MemotoReg,
  output RegfWrite,
  output MemRead,
  output MemWrite,
  output Branch,
  output ALUOp1,
  output ALUOp0
);

  wire not_1_out, not_2_out, not_3_out, not_4_out, not_5_out, not_6_out, not_7_out, not_8_out, not_9_out,
       not_10_out, not_11_out, not_12_out, not_13_out, not_14_out, not_15_out, not_16_out;

  not not_1 (not_1_out, op5);
  not not_2 (not_2_out, op4);
  not not_3 (not_3_out, op3);
  not not_4 (not_4_out, op2);
  not not_5 (not_5_out, op1);
  not not_6 (not_6_out, op0);
  and and_1 (ALUOp1, not_1_out, not_2_out, not_3_out, not_4_out, not_5_out, not_6_out);
  not not_7 (not_7_out, op4);
  not not_8 (not_8_out, op3);
  not not_9 (not_9_out, op2);
  and and_2 (MemotoReg, op5, not_7_out, not_8_out, not_9_out, op1, op0);
  not not_10 (not_10_out, op4);
  not not_11 (not_11_out, op2);
  and and_3 (MemWrite, op5, not_10_out, op3, not_11_out, op1, op0);
  not not_12 (not_12_out, op5);
  not not_13 (not_13_out, op4);
  not not_14 (not_14_out, op3);
  not not_15 (not_15_out, op1);
  not not_16 (not_16_out, op0);
  and and_4 (ALUOp0, not_12_out, not_13_out, not_14_out, op2, not_15_out, not_16_out);
  or or_1 (ALUSrc, MemotoReg, MemWrite);
  or or_2 (RegfWrite, ALUOp1, MemotoReg);

  assign Branch = ALUOp0;
  assign MemRead = MemotoReg;
  assign RegDst = ALUOp1;
endmodule

module one_bit_adder (
  input  a,
  input  b,
  input  carry_in,
  output sum,
  output carry_out
);

  wire and_1_out, and_2_out, and_3_out, and_4_out, and_5_out, and_6_out, and_7_out, not_1_out, not_2_out,
       not_3_out;

  not not_1 (not_1_out, a);
  not not_2 (not_2_out, b);
  not not_3 (not_3_out, carry_in);
  and and_1 (and_1_out, not_1_out, not_2_out, carry_in);
  and and_2 (and_2_out, not_1_out, b, not_3_out);
  and and_3 (and_3_out, a, not_2_out, not_3_out);
  and and_4 (and_4_out, a, b, carry_in);
  and and_5 (and_5_out, b, carry_in);
  and and_6 (and_6_out, a, carry_in);
  and and_7 (and_7_out, a, b);
  or or_1 (sum, and_1_out, and_2_out, and_3_out, and_4_out);
  or or_2 (carry_out, and_5_out, and_6_out, and_7_out);
  Dlatch dlatch_1 ();  // open: C, D, Q, Qbar
endmodule

module one_bit_alu (
  input  Ainvert,
  input  Binvert,
  input  Carry_in,
  input  [3:0] Operation,
  input  a,
  input  b,
  input  Less,
  output Result,
  output Set,
  output Overflow
);

  wire and_1_out, multiplexer_1_out, multiplexer_2_out, not_1_out, not_2_out, one_bit_adder_1_sum, or_1_out;

  not not_1 (not_1_out, a);
  not not_2 (not_2_out, b);
  Multiplexer multiplexer_1 (.in0(a), .in1(not_1_out), .out(multiplexer_1_out), .sel(Ainvert));
  Multiplexer multiplexer_2 (.in0(b), .in1(not_2_out), .out(multiplexer_2_out), .sel(Binvert));
  and and_1 (and_1_out, multiplexer_1_out, multiplexer_2_out);
  or or_1 (or_1_out, multiplexer_1_out, multiplexer_2_out);
  one_bit_adder one_bit_adder_1 (
    .a(multiplexer_1_out), .b(multiplexer_2_out), .carry_in(Carry_in), .sum(one_bit_adder_1_sum),
    .carry_out(Set));
  overflow_detect overflow_detect_1 (.a(multiplexer_1_out), .b(multiplexer_2_out), .cin(Set), .overflow(Overflow));
  Multiplexer #(.select(4)) multiplexer_3 (
    .in0(and_1_out), .in1(or_1_out), .in2(one_bit_adder_1_sum), .in3(Less), .in4(and_1_out),
    .in6(one_bit_adder_1_sum), .out(Result), .sel(Operation));  // open: in5, in7, in8, in9, in10, in11, in12, in13, in14, in15
endmodule

module therty_two_bit_alu (
  input  [3:0] Operation,
  input  [31:0] a,
  input  [31:0] b,
  output Zero,
  output [31:0] result,
  output Overflow
);

  wire Ainvert, Binvert, Carry_in, Less, one_bit_alu_1_set, one_bit_alu_2_set, one_bit_alu_3_set,
       one_bit_alu_4_set, one_bit_alu_5_set, one_bit_alu_6_set, one_bit_alu_7_set, one_bit_alu_8_set,
       one_bit_alu_9_set, one_bit_alu_10_set, one_bit_alu_11_set, one_bit_alu_12_set, one_bit_alu_13_set,
       one_bit_alu_14_set, one_bit_alu_15_set, one_bit_alu_16_set, one_bit_alu_17_set, one_bit_alu_18_set,
       one_bit_alu_19_set, one_bit_alu_20_set, one_bit_alu_21_set, one_bit_alu_22_set, one_bit_alu_23_set,
       one_bit_alu_24_set, one_bit_alu_25_set, one_bit_alu_26_set, one_bit_alu_27_set, one_bit_alu_28_set,
       one_bit_alu_29_set, one_bit_alu_30_set, one_bit_alu_31_set, one_bit_alu_32_set, or_1_out, or_2_out;
  wire [3:0] Operation_t;

  Option_menu_handler option_menu_handler_1 (
    .a3(Operation[3]), .a2(Operation[2]), .a1(Operation[1]), .a0(Operation[0]), .Ainverter(Ainvert),
    .Binverter(Binvert), .Carry_in(Carry_in), .op0(Operation_t[0]), .op1(Operation_t[1]),
    .op2(Operation_t[2]), .op3(Operation_t[3]));
  one_bit_alu one_bit_alu_1 (
    .Ainvert(Ainvert), .Binvert(Binvert), .Carry_in(Carry_in), .Operation(Operation_t), .a(a[0]), .b(b[0]),
    .Less(Less), .Result(result[0]), .Set(one_bit_alu_1_set));  // open: Overflow
  one_bit_alu one_bit_alu_2 (
    .Ainvert(Ainvert), .Binvert(Binvert), .Carry_in(one_bit_alu_1_set), .Operation(Operation_t), .a(a[1]),
    .b(b[1]), .Less(1'b0), .Result(result[1]), .Set(one_bit_alu_2_set));  // open: Overflow
  one_bit_alu one_bit_alu_3 (
    .Ainvert(Ainvert), .Binvert(Binvert), .Carry_in(one_bit_alu_2_set), .Operation(Operation_t), .a(a[2]),
    .b(b[2]), .Less(1'b0), .Result(result[2]), .Set(one_bit_alu_3_set));  // open: Overflow
  one_bit_alu one_bit_alu_4 (
    .Ainvert(Ainvert), .Binvert(Binvert), .Carry_in(one_bit_alu_3_set), .Operation(Operation_t), .a(a[3]),
    .b(b[3]), .Less(1'b0), .Result(result[3]), .Set(one_bit_alu_4_set));  // open: Overflow
  one_bit_alu one_bit_alu_5 (
    .Ainvert(Ainvert), .Binvert(Binvert), .Carry_in(one_bit_alu_4_set), .Operation(Operation_t), .a(a[4]),
    .b(b[4]), .Less(1'b0), .Result(result[4]), .Set(one_bit_alu_5_set));  // open: Overflow
  one_bit_alu one_bit_alu_6 (
    .Ainvert(Ainvert), .Binvert(Binvert), .Carry_in(one_bit_alu_5_set), .Operation(Operation_t), .a(a[5]),
    .b(b[5]), .Less(1'b0), .Result(result[5]), .Set(one_bit_alu_6_set));  // open: Overflow
  one_bit_alu one_bit_alu_7 (
    .Ainvert(Ainvert), .Binvert(Binvert), .Carry_in(one_bit_alu_6_set), .Operation(Operation_t), .a(a[6]),
    .b(b[6]), .Less(1'b0), .Result(result[6]), .Set(one_bit_alu_7_set));  // open: Overflow
  one_bit_alu one_bit_alu_8 (
    .Ainvert(Ainvert), .Binvert(Binvert), .Carry_in(one_bit_alu_7_set), .Operation(Operation_t), .a(a[7]),
    .b(b[7]), .Less(1'b0), .Result(result[7]), .Set(one_bit_alu_8_set));  // open: Overflow
  one_bit_alu one_bit_alu_9 (
    .Ainvert(Ainvert), .Binvert(Binvert), .Carry_in(one_bit_alu_8_set), .Operation(Operation_t), .a(a[8]),
    .b(b[8]), .Less(1'b0), .Result(result[8]), .Set(one_bit_alu_9_set));  // open: Overflow
  one_bit_alu one_bit_alu_10 (
    .Ainvert(Ainvert), .Binvert(Binvert), .Carry_in(one_bit_alu_9_set), .Operation(Operation_t), .a(a[9]),
    .b(b[9]), .Less(1'b0), .Result(result[9]), .Set(one_bit_alu_10_set));  // open: Overflow
  one_bit_alu one_bit_alu_11 (
    .Ainvert(Ainvert), .Binvert(Binvert), .Carry_in(one_bit_alu_10_set), .Operation(Operation_t), .a(a[10]),
    .b(b[10]), .Less(1'b0), .Result(result[10]), .Set(one_bit_alu_11_set));  // open: Overflow
  one_bit_alu one_bit_alu_12 (
    .Ainvert(Ainvert), .Binvert(Binvert), .Carry_in(one_bit_alu_11_set), .Operation(Operation_t), .a(a[11]),
    .b(b[11]), .Less(1'b0), .Result(result[11]), .Set(one_bit_alu_12_set));  // open: Overflow
  one_bit_alu one_bit_alu_13 (
    .Ainvert(Ainvert), .Binvert(Binvert), .Carry_in(one_bit_alu_12_set), .Operation(Operation_t), .a(a[12]),
    .b(b[12]), .Less(1'b0), .Result(result[12]), .Set(one_bit_alu_13_set));  // open: Overflow
  one_bit_alu one_bit_alu_14 (
    .Ainvert(Ainvert), .Binvert(Binvert), .Carry_in(one_bit_alu_13_set), .Operation(Operation_t), .a(a[13]),
    .b(b[13]), .Less(1'b0), .Result(result[13]), .Set(one_bit_alu_14_set));  // open: Overflow
  one_bit_alu one_bit_alu_15 (
    .Ainvert(Ainvert), .Binvert(Binvert), .Carry_in(one_bit_alu_14_set), .Operation(Operation_t), .a(a[14]),
    .b(b[14]), .Less(1'b0), .Result(result[14]), .Set(one_bit_alu_15_set));  // open: Overflow
  one_bit_alu one_bit_alu_16 (
    .Ainvert(Ainvert), .Binvert(Binvert), .Carry_in(one_bit_alu_15_set), .Operation(Operation_t), .a(a[15]),
    .b(b[15]), .Less(1'b0), .Result(result[15]), .Set(one_bit_alu_16_set));  // open: Overflow
  one_bit_alu one_bit_alu_17 (
    .Ainvert(Ainvert), .Binvert(Binvert), .Carry_in(one_bit_alu_16_set), .Operation(Operation_t), .a(a[16]),
    .b(b[16]), .Less(1'b0), .Result(result[16]), .Set(one_bit_alu_17_set));  // open: Overflow
  one_bit_alu one_bit_alu_18 (
    .Ainvert(Ainvert), .Binvert(Binvert), .Carry_in(one_bit_alu_17_set), .Operation(Operation_t), .a(a[17]),
    .b(b[17]), .Less(1'b0), .Result(result[17]), .Set(one_bit_alu_18_set));  // open: Overflow
  one_bit_alu one_bit_alu_19 (
    .Ainvert(Ainvert), .Binvert(Binvert), .Carry_in(one_bit_alu_18_set), .Operation(Operation_t), .a(a[18]),
    .b(b[18]), .Less(1'b0), .Result(result[18]), .Set(one_bit_alu_19_set));  // open: Overflow
  one_bit_alu one_bit_alu_20 (
    .Ainvert(Ainvert), .Binvert(Binvert), .Carry_in(one_bit_alu_19_set), .Operation(Operation_t), .a(a[19]),
    .b(b[19]), .Less(1'b0), .Result(result[19]), .Set(one_bit_alu_20_set));  // open: Overflow
  one_bit_alu one_bit_alu_21 (
    .Ainvert(Ainvert), .Binvert(Binvert), .Carry_in(one_bit_alu_20_set), .Operation(Operation_t), .a(a[20]),
    .b(b[20]), .Less(1'b0), .Result(result[20]), .Set(one_bit_alu_21_set));  // open: Overflow
  one_bit_alu one_bit_alu_22 (
    .Ainvert(Ainvert), .Binvert(Binvert), .Carry_in(one_bit_alu_21_set), .Operation(Operation_t), .a(a[21]),
    .b(b[21]), .Less(1'b0), .Result(result[21]), .Set(one_bit_alu_22_set));  // open: Overflow
  one_bit_alu one_bit_alu_23 (
    .Ainvert(Ainvert), .Binvert(Binvert), .Carry_in(one_bit_alu_22_set), .Operation(Operation_t), .a(a[22]),
    .b(b[22]), .Less(1'b0), .Result(result[22]), .Set(one_bit_alu_23_set));  // open: Overflow
  one_bit_alu one_bit_alu_24 (
    .Ainvert(Ainvert), .Binvert(Binvert), .Carry_in(one_bit_alu_23_set), .Operation(Operation_t), .a(a[23]),
    .b(b[23]), .Less(1'b0), .Result(result[23]), .Set(one_bit_alu_24_set));  // open: Overflow
  one_bit_alu one_bit_alu_25 (
    .Ainvert(Ainvert), .Binvert(Binvert), .Carry_in(one_bit_alu_24_set), .Operation(Operation_t), .a(a[24]),
    .b(b[24]), .Less(1'b0), .Result(result[24]), .Set(one_bit_alu_25_set));  // open: Overflow
  one_bit_alu one_bit_alu_26 (
    .Ainvert(Ainvert), .Binvert(Binvert), .Carry_in(one_bit_alu_25_set), .Operation(Operation_t), .a(a[25]),
    .b(b[25]), .Less(1'b0), .Result(result[25]), .Set(one_bit_alu_26_set));  // open: Overflow
  one_bit_alu one_bit_alu_27 (
    .Ainvert(Ainvert), .Binvert(Binvert), .Carry_in(one_bit_alu_26_set), .Operation(Operation_t), .a(a[26]),
    .b(b[26]), .Less(1'b0), .Result(result[26]), .Set(one_bit_alu_27_set));  // open: Overflow
  one_bit_alu one_bit_alu_28 (
    .Ainvert(Ainvert), .Binvert(Binvert), .Carry_in(one_bit_alu_27_set), .Operation(Operation_t), .a(a[27]),
    .b(b[27]), .Less(1'b0), .Result(result[27]), .Set(one_bit_alu_28_set));  // open: Overflow
  one_bit_alu one_bit_alu_29 (
    .Ainvert(Ainvert), .Binvert(Binvert), .Carry_in(one_bit_alu_28_set), .Operation(Operation_t), .a(a[28]),
    .b(b[28]), .Less(1'b0), .Result(result[28]), .Set(one_bit_alu_29_set));  // open: Overflow
  one_bit_alu one_bit_alu_30 (
    .Ainvert(Ainvert), .Binvert(Binvert), .Carry_in(one_bit_alu_29_set), .Operation(Operation_t), .a(a[29]),
    .b(b[29]), .Less(1'b0), .Result(result[29]), .Set(one_bit_alu_30_set));  // open: Overflow
  one_bit_alu one_bit_alu_31 (
    .Ainvert(Ainvert), .Binvert(Binvert), .Carry_in(one_bit_alu_30_set), .Operation(Operation_t), .a(a[30]),
    .b(b[30]), .Less(1'b0), .Result(result[30]), .Set(one_bit_alu_31_set));  // open: Overflow
  one_bit_alu one_bit_alu_32 (
    .Ainvert(Ainvert), .Binvert(Binvert), .Carry_in(one_bit_alu_31_set), .Operation(Operation_t), .a(a[31]),
    .b(b[31]), .Less(1'b0), .Result(result[31]), .Set(one_bit_alu_32_set), .Overflow(Overflow));
  or or_1 (or_1_out, Overflow, one_bit_alu_32_set);
  not not_1 (Less, or_1_out);
  or or_2 (or_2_out, result[0], result[1], result[2], result[3], result[10], result[9], result[8], result[7], result[8], result[9], result[10], result[11], result[12], result[13], result[14], result[15], result[4], result[16], result[17], result[18], result[31], result[30], result[29], result[28], result[27], result[26], result[25], result[24], result[23], result[22], result[21], result[20], result[19]);
  not not_2 (Zero, or_2_out);
endmodule

module Option_menu_handler (
  input  a3,
  input  a2,
  input  a1,
  input  a0,
  output Ainverter,
  output Binverter,
  output Carry_in,
  output op0,
  output op1,
  output op2,
  output op3
);

  wire and_2_out, and_3_out, and_4_out, and_5_out, and_6_out, and_7_out, and_8_out, not_1_out, not_2_out,
       not_3_out, not_4_out;

  not not_1 (not_1_out, a3);
  not not_2 (not_2_out, a2);
  not not_3 (not_3_out, a1);
  not not_4 (not_4_out, a0);
  and and_1 (Ainverter, not_1_out, a2, not_3_out, not_4_out);
  and and_2 (and_2_out, not_1_out, not_2_out, a1, a0);
  and and_3 (and_3_out, not_1_out, a2, not_4_out);
  and and_4 (and_4_out, not_1_out, not_2_out, a1, a0);
  and and_5 (and_5_out, not_1_out, a2, a1, not_4_out);
  and and_6 (and_6_out, a2, not_3_out);
  and and_7 (and_7_out, a2, a0);
  and and_8 (and_8_out, a3, a2);
  or or_1 (Binverter, and_2_out, and_3_out);
  or or_2 (Carry_in, and_4_out, and_5_out);
  or or_3 (op2, and_6_out, and_7_out, and_8_out);

  assign op0 = a0;
  assign op1 = a1;
  assign op3 = a3;
endmodule

module overflow_detect (
  input  a,
  input  b,
  input  cin,
  output overflow
);

  wire and_1_out, and_2_out, and_3_out;

  and and_1 (and_1_out, b, cin);
  and and_2 (and_2_out, a, cin);
  and and_3 (and_3_out, a, b);
  or or_1 (overflow, and_1_out, and_2_out, and_3_out);
endmodule

module Dlatch (
  input  C,
  input  D,
  output Q,
  output Qbar
);

  wire and_1_out, and_2_out, not_1_out;

  and and_1 (and_1_out, C, not_1_out);
  not not_1 (not_1_out, D);
  and and_2 (and_2_out, C, D);
  nor nor_1 (Q, and_1_out, Qbar);
  nor nor_2 (Qbar, Q, and_2_out);
endmodule

module Dflipflop (
  input  C,
  input  D,
  output Q,
  output Qbar
);

  wire dlatch_1_q, not_1_out;

  not not_1 (not_1_out, C);
  Dlatch dlatch_1 (.C(C), .D(D), .Q(dlatch_1_q));  // open: Qbar
  Dlatch dlatch_2 (.C(not_1_out), .D(dlatch_1_q), .Q(Q), .Qbar(Qbar));
endmodule

module regster (
  input  C,
  input  [31:0] D,
  output [31:0] Q
);

  Dflipflop dflipflop_1 (.C(C), .D(D[0]), .Q(Q[0]));  // open: Qbar
  Dflipflop dflipflop_2 (.C(C), .D(D[1]), .Q(Q[1]));  // open: Qbar
  Dflipflop dflipflop_3 (.C(C), .D(D[2]), .Q(Q[2]));  // open: Qbar
  Dflipflop dflipflop_4 (.C(C), .D(D[3]), .Q(Q[3]));  // open: Qbar
  Dflipflop dflipflop_5 (.C(C), .D(D[4]), .Q(Q[4]));  // open: Qbar
  Dflipflop dflipflop_6 (.C(C), .D(D[5]), .Q(Q[5]));  // open: Qbar
  Dflipflop dflipflop_7 (.C(C), .D(D[6]), .Q(Q[6]));  // open: Qbar
  Dflipflop dflipflop_8 (.C(C), .D(D[7]), .Q(Q[7]));  // open: Qbar
  Dflipflop dflipflop_9 (.C(C), .D(D[8]), .Q(Q[8]));  // open: Qbar
  Dflipflop dflipflop_10 (.C(C), .D(D[9]), .Q(Q[9]));  // open: Qbar
  Dflipflop dflipflop_11 (.C(C), .D(D[10]), .Q(Q[10]));  // open: Qbar
  Dflipflop dflipflop_12 (.C(C), .D(D[11]), .Q(Q[11]));  // open: Qbar
  Dflipflop dflipflop_13 (.C(C), .D(D[12]), .Q(Q[12]));  // open: Qbar
  Dflipflop dflipflop_14 (.C(C), .D(D[13]), .Q(Q[13]));  // open: Qbar
  Dflipflop dflipflop_15 (.C(C), .D(D[14]), .Q(Q[14]));  // open: Qbar
  Dflipflop dflipflop_16 (.C(C), .D(D[15]), .Q(Q[15]));  // open: Qbar
  Dflipflop dflipflop_17 (.C(C), .D(D[16]), .Q(Q[16]));  // open: Qbar
  Dflipflop dflipflop_18 (.C(C), .D(D[17]), .Q(Q[17]));  // open: Qbar
  Dflipflop dflipflop_19 (.C(C), .D(D[18]), .Q(Q[18]));  // open: Qbar
  Dflipflop dflipflop_20 (.C(C), .D(D[19]), .Q(Q[19]));  // open: Qbar
  Dflipflop dflipflop_21 (.C(C), .D(D[20]), .Q(Q[20]));  // open: Qbar
  Dflipflop dflipflop_22 (.C(C), .D(D[21]), .Q(Q[21]));  // open: Qbar
  Dflipflop dflipflop_23 (.C(C), .D(D[22]), .Q(Q[22]));  // open: Qbar
  Dflipflop dflipflop_24 (.C(C), .D(D[23]), .Q(Q[23]));  // open: Qbar
  Dflipflop dflipflop_25 (.C(C), .D(D[24]), .Q(Q[24]));  // open: Qbar
  Dflipflop dflipflop_26 (.C(C), .D(D[25]), .Q(Q[25]));  // open: Qbar
  Dflipflop dflipflop_27 (.C(C), .D(D[26]), .Q(Q[26]));  // open: Qbar
  Dflipflop dflipflop_28 (.C(C), .D(D[27]), .Q(Q[27]));  // open: Qbar
  Dflipflop dflipflop_29 (.C(C), .D(D[28]), .Q(Q[28]));  // open: Qbar
  Dflipflop dflipflop_30 (.C(C), .D(D[29]), .Q(Q[29]));  // open: Qbar
  Dflipflop dflipflop_31 (.C(C), .D(D[30]), .Q(Q[30]));  // open: Qbar
  Dflipflop dflipflop_32 (.C(C), .D(D[31]), .Q(Q[31]));  // open: Qbar
endmodule

module fileregister (
  input  WriteSignl,
  input  [4:0] registre1,
  input  [4:0] registre2,
  input  [4:0] regWrite,
  input  [31:0] DataWrite,
  output [31:0] data1,
  output [31:0] data2
);

  wire and_1_out, and_2_out, and_3_out, and_4_out, and_5_out, and_6_out, and_7_out, and_8_out, and_9_out,
       and_10_out, and_11_out, and_12_out, and_13_out, and_14_out, and_15_out, and_16_out, and_17_out,
       and_18_out, and_19_out, and_20_out, and_21_out, and_22_out, and_23_out, and_24_out, and_25_out,
       and_26_out, and_27_out, and_28_out, and_29_out, and_30_out, and_31_out, and_32_out, decoder_1_out0,
       decoder_1_out1, decoder_1_out2, decoder_1_out3, decoder_1_out4, decoder_1_out5, decoder_1_out6,
       decoder_1_out7, decoder_1_out8, decoder_1_out9, decoder_1_out10, decoder_1_out11, decoder_1_out12,
       decoder_1_out13, decoder_1_out14, decoder_1_out15, decoder_1_out16, decoder_1_out17, decoder_1_out18,
       decoder_1_out19, decoder_1_out20, decoder_1_out21, decoder_1_out22, decoder_1_out23, decoder_1_out24,
       decoder_1_out25, decoder_1_out26, decoder_1_out27, decoder_1_out28, decoder_1_out29, decoder_1_out30,
       decoder_1_out31;
  wire [31:0] regster_1_q, regster_2_q, regster_3_q, regster_4_q, regster_5_q, regster_6_q, regster_7_q,
       regster_8_q, regster_9_q, regster_10_q, regster_11_q, regster_12_q, regster_13_q, regster_14_q,
       regster_15_q, regster_16_q, regster_17_q, regster_18_q, regster_19_q, regster_20_q, regster_21_q,
       regster_22_q, regster_23_q, regster_24_q, regster_25_q, regster_26_q, regster_27_q, regster_28_q,
       regster_29_q, regster_30_q, regster_31_q, regster_32_q;

  Decoder #(.select(5)) decoder_1 (
    .out0(decoder_1_out0), .out1(decoder_1_out1), .out2(decoder_1_out2), .out3(decoder_1_out3),
    .out4(decoder_1_out4), .out5(decoder_1_out5), .out6(decoder_1_out6), .out7(decoder_1_out7),
    .out8(decoder_1_out8), .out9(decoder_1_out9), .out10(decoder_1_out10), .out11(decoder_1_out11),
    .out12(decoder_1_out12), .out13(decoder_1_out13), .out14(decoder_1_out14), .out15(decoder_1_out15),
    .out16(decoder_1_out16), .out17(decoder_1_out17), .out18(decoder_1_out18), .out19(decoder_1_out19),
    .out20(decoder_1_out20), .out21(decoder_1_out21), .out22(decoder_1_out22), .out23(decoder_1_out23),
    .out24(decoder_1_out24), .out25(decoder_1_out25), .out26(decoder_1_out26), .out27(decoder_1_out27),
    .out28(decoder_1_out28), .out29(decoder_1_out29), .out30(decoder_1_out30), .out31(decoder_1_out31),
    .sel(regWrite));  // open: en
  and and_1 (and_1_out, WriteSignl, decoder_1_out0);
  and and_2 (and_2_out, WriteSignl, decoder_1_out1);
  and and_3 (and_3_out, WriteSignl, decoder_1_out2);
  and and_4 (and_4_out, WriteSignl, decoder_1_out3);
  and and_5 (and_5_out, WriteSignl, decoder_1_out4);
  and and_6 (and_6_out, WriteSignl, decoder_1_out5);
  and and_7 (and_7_out, WriteSignl, decoder_1_out6);
  and and_8 (and_8_out, WriteSignl, decoder_1_out7);
  and and_9 (and_9_out, WriteSignl, decoder_1_out8);
  and and_10 (and_10_out, WriteSignl, decoder_1_out9);
  and and_11 (and_11_out, WriteSignl, decoder_1_out10);
  and and_12 (and_12_out, WriteSignl, decoder_1_out11);
  and and_13 (and_13_out, WriteSignl, decoder_1_out12);
  and and_14 (and_14_out, WriteSignl, decoder_1_out13);
  and and_15 (and_15_out, WriteSignl, decoder_1_out14);
  and and_16 (and_16_out, WriteSignl, decoder_1_out15);
  and and_17 (and_17_out, WriteSignl, decoder_1_out16);
  and and_18 (and_18_out, WriteSignl, decoder_1_out17);
  and and_19 (and_19_out, WriteSignl, decoder_1_out18);
  and and_20 (and_20_out, WriteSignl, decoder_1_out19);
  and and_21 (and_21_out, WriteSignl, decoder_1_out20);
  and and_22 (and_22_out, WriteSignl, decoder_1_out21);
  and and_23 (and_23_out, WriteSignl, decoder_1_out22);
  and and_24 (and_24_out, WriteSignl, decoder_1_out23);
  and and_25 (and_25_out, WriteSignl, decoder_1_out24);
  and and_26 (and_26_out, WriteSignl, decoder_1_out25);
  and and_27 (and_27_out, WriteSignl, decoder_1_out26);
  and and_28 (and_28_out, WriteSignl, decoder_1_out27);
  and and_29 (and_29_out, WriteSignl, decoder_1_out28);
  and and_30 (and_30_out, WriteSignl, decoder_1_out29);
  and and_31 (and_31_out, WriteSignl, decoder_1_out30);
  and and_32 (and_32_out, WriteSignl, decoder_1_out31);
  regster regster_1 (.C(and_1_out), .D(DataWrite), .Q(regster_1_q));
  regster regster_2 (.C(and_2_out), .D(DataWrite), .Q(regster_2_q));
  regster regster_3 (.C(and_3_out), .D(DataWrite), .Q(regster_3_q));
  regster regster_4 (.C(and_4_out), .D(DataWrite), .Q(regster_4_q));
  regster regster_5 (.C(and_5_out), .D(DataWrite), .Q(regster_5_q));
  regster regster_6 (.C(and_6_out), .D(DataWrite), .Q(regster_6_q));
  regster regster_7 (.C(and_7_out), .D(DataWrite), .Q(regster_7_q));
  regster regster_8 (.C(and_8_out), .D(DataWrite), .Q(regster_8_q));
  regster regster_9 (.C(and_9_out), .D(DataWrite), .Q(regster_9_q));
  regster regster_10 (.C(and_10_out), .D(DataWrite), .Q(regster_10_q));
  regster regster_11 (.C(and_11_out), .D(DataWrite), .Q(regster_11_q));
  regster regster_12 (.C(and_12_out), .D(DataWrite), .Q(regster_12_q));
  regster regster_13 (.C(and_13_out), .D(DataWrite), .Q(regster_13_q));
  regster regster_14 (.C(and_14_out), .D(DataWrite), .Q(regster_14_q));
  regster regster_15 (.C(and_15_out), .D(DataWrite), .Q(regster_15_q));
  regster regster_16 (.C(and_16_out), .D(DataWrite), .Q(regster_16_q));
  regster regster_17 (.C(and_17_out), .D(DataWrite), .Q(regster_17_q));
  regster regster_18 (.C(and_18_out), .D(DataWrite), .Q(regster_18_q));
  regster regster_19 (.C(and_19_out), .D(DataWrite), .Q(regster_19_q));
  regster regster_20 (.C(and_20_out), .D(DataWrite), .Q(regster_20_q));
  regster regster_21 (.C(and_21_out), .D(DataWrite), .Q(regster_21_q));
  regster regster_22 (.C(and_22_out), .D(DataWrite), .Q(regster_22_q));
  regster regster_23 (.C(and_23_out), .D(DataWrite), .Q(regster_23_q));
  regster regster_24 (.C(and_24_out), .D(DataWrite), .Q(regster_24_q));
  regster regster_25 (.C(and_25_out), .D(DataWrite), .Q(regster_25_q));
  regster regster_26 (.C(and_26_out), .D(DataWrite), .Q(regster_26_q));
  regster regster_27 (.C(and_27_out), .D(DataWrite), .Q(regster_27_q));
  regster regster_28 (.C(and_28_out), .D(DataWrite), .Q(regster_28_q));
  regster regster_29 (.C(and_29_out), .D(DataWrite), .Q(regster_29_q));
  regster regster_30 (.C(and_30_out), .D(DataWrite), .Q(regster_30_q));
  regster regster_31 (.C(and_31_out), .D(DataWrite), .Q(regster_31_q));
  regster regster_32 (.C(and_32_out), .D(DataWrite), .Q(regster_32_q));
  Multiplexer #(.select(5), .width(32)) multiplexer_1 (
    .in0(regster_1_q), .in1(regster_2_q), .in2(regster_3_q), .in3(regster_4_q), .in4(regster_5_q),
    .in5(regster_6_q), .in6(regster_7_q), .in7(regster_8_q), .in8(regster_9_q), .in9(regster_10_q),
    .in10(regster_11_q), .in11(regster_12_q), .in12(regster_13_q), .in13(regster_14_q), .in14(regster_15_q),
    .in15(regster_16_q), .in16(regster_17_q), .in17(regster_18_q), .in18(regster_19_q), .in19(regster_20_q),
    .in20(regster_21_q), .in21(regster_22_q), .in22(regster_23_q), .in23(regster_24_q), .in24(regster_25_q),
    .in25(regster_26_q), .in26(regster_27_q), .in27(regster_28_q), .in28(regster_29_q), .in29(regster_30_q),
    .in30(regster_31_q), .in31(regster_32_q), .out(data1), .sel(registre1));
  Multiplexer #(.select(5), .width(32)) multiplexer_2 (
    .in0(regster_1_q), .in1(regster_2_q), .in2(regster_3_q), .in3(regster_4_q), .in4(regster_5_q),
    .in5(regster_6_q), .in6(regster_7_q), .in7(regster_8_q), .in8(regster_9_q), .in9(regster_10_q),
    .in10(regster_11_q), .in11(regster_12_q), .in12(regster_13_q), .in13(regster_14_q), .in14(regster_15_q),
    .in15(regster_16_q), .in16(regster_17_q), .in17(regster_18_q), .in18(regster_19_q), .in19(regster_20_q),
    .in20(regster_21_q), .in21(regster_22_q), .in22(regster_23_q), .in23(regster_24_q), .in24(regster_25_q),
    .in25(regster_26_q), .in26(regster_27_q), .in27(regster_28_q), .in28(regster_29_q), .in29(regster_30_q),
    .in30(regster_31_q), .in31(regster_32_q), .out(data2), .sel(registre2));
endmodule

module ImmGen (
  input  [11:0] imm,
  output [31:0] out_2
);


  assign out_2 = {{20{1'b0}}, imm};

  // Notes on the sheet:
  //   Simple immediate genration
endmodule

module PC (
  input  Clk,
  input  [31:0] in_2,
  output [31:0] out_3
);

  wire and_1_out;

  and and_1 (and_1_out, Clk, 1'b1);
  Multiplexer #(.width(32)) multiplexer_1 (.in0({32{1'b0}}), .in1(in_2), .out(out_3), .sel(and_1_out));

  // Notes on the sheet:
  //   Simple PC simulatior
endmodule

module cut (
  input  [31:0] in_1,
  output [7:0] out_2
);


  assign out_2 = in_1[7:0];
endmodule
