// Logisim project ControlBlock.circ as structural Verilog: 3 circuits, main circuit main
module main (
  input  in_1,
  input  in_2,
  input  in_3,
  input  in_4,
  input  in_5,
  input  in_6,
  output Desitnation_sig,
  output AluSource_sig,
  output MemOut_sig,
  output WriteReg_sig,
  output ReadMem_sig,
  output WriteMem_sig,
  output Br_sig,
  output [3:0] Operation
);

  wire maincontrol_1_aluop0, maincontrol_1_aluop1;

  MainControl maincontrol_1 (
    .op5(in_1), .op4(in_2), .op3(in_3), .op2(in_4), .op1(in_5), .op0(in_6), .RegDst(Desitnation_sig),
    .ALUSrc(AluSource_sig), .MemotoReg(MemOut_sig), .RegfWrite(WriteReg_sig), .MemRead(ReadMem_sig),
    .MemWrite(WriteMem_sig), .Branch(Br_sig), .ALUOp1(maincontrol_1_aluop1), .ALUOp0(maincontrol_1_aluop0));
  ALUControl alucontrol_1 (
    .ALUOp1(maincontrol_1_aluop1), .ALUOp0(maincontrol_1_aluop0), .Functs({in_3, in_4, in_5, in_6}),
    .Operation(Operation));

  // Notes on the sheet:
  //   These circuite is developed by Student.Ahmed Fouatih Hamza Faiz 
  //   Archi-2    winter-2025
endmodule

module ALUControl (
  input  ALUOp1,
  input  ALUOp0,
  input  [3:0] Functs,
  output [3:0] Operation
);

  wire and_1_out, not_1_out, not_2_out, not_3_out, or_1_out;

  or or_1 (or_1_out, Functs[3], Functs[0]);
  and and_1 (and_1_out, ALUOp1, Functs[1]);
  and and_2 (Operation[0], ALUOp1, or_1_out);
  and and_3 (Operation[3], ALUOp0, not_1_out);
  not not_1 (not_1_out, ALUOp0);
  or or_2 (Operation[2], ALUOp0, and_1_out);
  not not_2 (not_2_out, ALUOp1);
  or or_3 (Operation[1], not_2_out, not_3_out);
  not not_3 (not_3_out, Functs[2]);
endmodule

module MainControl (
  input  op5,
  input  op4,
  input  op3,
  input  op2,
  input  op1,
  input  op0,
  output RegDst,
  output ALUSrc,
  output MemotoReg,
  output RegfWrite,
  output MemRead,
  output MemWrite,
  output Branch,
  output ALUOp1,
  output ALUOp0
);

  wire not_1_out, not_2_out, not_3_out, not_4_out, not_5_out, not_6_out, not_7_out, not_8_out, not_9_out,
       not_10_out, not_11_out, not_12_out, not_13_out, not_14_out, not_15_out, not_16_out;

  not not_1 (not_1_out, op5);
  not not_2 (not_2_out, op4);
  not not_3 (not_3_out, op3);
  not not_4 (not_4_out, op2);
  not not_5 (not_5_out, op1);
  not not_6 (not_6_out, op0);
  and and_1 (ALUOp1, not_1_out, not_2_out, not_3_out, not_4_out, not_5_out, not_6_out);
  not not_7 (not_7_out, op4);
  not not_8 (not_8_out, op3);
  not not_9 (not_9_out, op2);
  and and_2 (MemotoReg, op5, not_7_out, not_8_out, not_9_out, op1, op0);
  not not_10 (not_10_out, op4);
  not not_11 (not_11_out, op2);
  and and_3 (MemWrite, op5, not_10_out, op3, not_11_out, op1, op0);
  not not_12 (not_12_out, op5);
  not not_13 (not_13_out, op4);
  not not_14 (not_14_out, op3);
  not not_15 (not_15_out, op1);
  not not_16 (not_16_out, op0);
  and and_4 (ALUOp0, not_12_out, not_13_out, not_14_out, op2, not_15_out, not_16_out);
  or or_1 (ALUSrc, MemotoReg, MemWrite);
  or or_2 (RegfWrite, ALUOp1, MemotoReg);

  assign Branch = ALUOp0;
  assign MemRead = MemotoReg;
  assign RegDst = ALUOp1;
endmodule
