// Logisim project Displaying_1.circ as structural Verilog: 2 circuits, main circuit main
module main (
);

  wire Ask_out, displaying_1_ttyclk, displaying_1_ttyclr;
  wire [6:0] displaying_1_ttyout;

  Button Ask (.out(Ask_out));
  Displaying displaying_1 (
    .rst(Ask_out), .ttyOut(displaying_1_ttyout), .ttyClk(displaying_1_ttyclk), .ttyClr(displaying_1_ttyclr));
  TTY #(.cols(50), .rows(20)) tty_1 (
    .data(displaying_1_ttyout), .clk(displaying_1_ttyclk), .clr(displaying_1_ttyclr));  // open: we
endmodule

module Displaying (
  input  rst,
  output [6:0] ttyOut,
  output ttyClk,
  output ttyClr
);

  wire ena, not_1_out, or_1_out;
  wire [7:7] rom_1_data;
  wire [11:0] counter_1_q;

  or or_1 (or_1_out, ttyClk, ttyClr);
  Counter #(.max('hfff), .width(12)) counter_1 (
    .load(ttyClr), .count(ena), .clk(or_1_out), .D({12{1'b0}}), .Q(counter_1_q));  // open: clr, up, carry
  ROM #(.addrWidth(12)) rom_1 (.addr(counter_1_q), .data({rom_1_data[7], ttyOut}));
  not not_1 (not_1_out, ena);
  and and_1 (ttyClr, rst, not_1_out);
  BitFinder #(.width(7)) bitfinder_1 (.in(ttyOut), .found(ena));  // open: index
  Clock #(.lowDuration(5)) clock_1 (.out(ttyClk));

  // Other names for the same wires on the sheet: ctrClk = ttyClk; load = ttyClr

  // Notes on the sheet:
  //   contents of rom_1 (hex, n*v repeats v):
  //   4d 79 20 6e 61 6d 65 20 69 73 3a 20 41 48 4d 45 44 20 46 4f 55 41 54 49 48 20 48 41 4d 5a 41 20 46
  //   41 49 5a a 23*2a a 49 20 61 6d 3a 20 31 39 20 79 65 61 72 73 20 6f 6c 64 a 25*2b a 49 20 67 6f 74 20
  //   31 35 20 69 6e 20 44 61 74 61 62 61 73 65 2e a 8*14 13 a 49 20 67 6f 74 20 31 34 20 69 6e 20 57 65
  //   62 44 65 76 2e a 26*2f a 49 20 67 6f 74 20 31 35 20 69 6e 20 4d 61 74 68 2e a 27*2a a 49 20 67 6f 74
  //   20 31 35 20 69 6e 20 74 68 65 20 6f 74 68 65 72 20 6d 61 74 68 20 6d 6f 64 75 6c 65 2e
endmodule
