// Logisim project LIGHT_UP.circ as structural Verilog
module LIGHT (
);

  wire a, b, c, clock_1_out, d, e, GRN, GRN1, ORG, ORG1, RED, RED1, S1, s1_t, S2, s2_t, S3, s3_t, S4, s4_t,
       S5, s5_t, S6, s6_t, S7, s7_t;

  Clock clock_1 (.out(clock_1_out));
  Counter #(.max('h1f), .width(5)) counter_1 (
    .clk(clock_1_out), .Q({a, b, c, d, e}));  // open: clr, load, up, count, D, carry
  ROM #(.addrWidth(5), .dataWidth(3)) rom_1 (.addr({a, b, c, d, e}), .data({ORG, GRN, RED}));
  SEGMENT0_1 segment0_1_1 (
    .a(a), .b(b), .c(c), .d(d), .e(e), .s1(S1), .s2(S2), .s3(S3), .s4(S4), .s5(S5), .s6(S6), .s7(S7));
  _7_Segment_Display u_7_segment_display_1 (.g(S7), .f(S2), .a(S1), .b(S4), .e(S5), .d(S6), .c(S3));  // open: dp
  _7_Segment_Display u_7_segment_display_2 (
    .g(s7_t), .f(s2_t), .a(s1_t), .b(s3_t), .e(s6_t), .d(s5_t), .c(s4_t));  // open: dp
  LED led_1 (.in(GRN1));
  LED led_2 (.in(RED));
  LED led_3 (.in(ORG));
  LED led_4 (.in(GRN));
  LED led_5 (.in(GRN1));
  SEGMENT1_9 segment1_9_1 (
    .a(a), .b(b), .c(c), .d(d), .e(e), .s1(s1_t), .s2(s2_t), .s3(s3_t), .s4(s4_t), .s5(s5_t), .s6(s6_t),
    .s7(s7_t));
  LED led_6 (.in(ORG1));
  LED led_7 (.in(RED1));
  LED led_8 (.in(ORG1));
  LED led_9 (.in(RED1));
  _7_Segment_Display u_7_segment_display_3 (.g(S7), .f(S2), .a(S1), .b(S4), .e(S5), .d(S6), .c(S3));  // open: dp
  LED led_10 (.in(RED));
  LED led_11 (.in(ORG));
  LED led_12 (.in(GRN));
  _7_Segment_Display u_7_segment_display_4 (.g(S7), .f(S2), .a(S1), .b(S4), .e(S5), .d(S6), .c(S3));  // open: dp
  _7_Segment_Display u_7_segment_display_5 (
    .g(s7_t), .f(s2_t), .a(s1_t), .b(s3_t), .e(s6_t), .d(s5_t), .c(s4_t));  // open: dp
  _7_Segment_Display u_7_segment_display_6 (
    .g(s7_t), .f(s2_t), .a(s1_t), .b(s3_t), .e(s6_t), .d(s5_t), .c(s4_t));  // open: dp
  _7_Segment_Display u_7_segment_display_7 (.g(S7), .f(S2), .a(S1), .b(S4), .e(S5), .d(S6), .c(S3));  // open: dp
  HANDL_IT handl_it_1 (.a(a), .b(b), .c(c), .d(d), .e(e), .x(GRN1), .y(ORG1), .z(RED1));
  _7_Segment_Display u_7_segment_display_8 (
    .g(s7_t), .f(s2_t), .a(s1_t), .b(s3_t), .e(s6_t), .d(s5_t), .c(s4_t));  // open: dp

  // Notes on the sheet:
  //   contents of rom_1 (hex, n*v repeats v):
  //   16*1 12*2 4*4
endmodule

module SEGMENT1_9 (
  input  a,
  input  b,
  input  c,
  input  d,
  input  e,
  output s1,
  output s2,
  output s3,
  output s4,
  output s5,
  output s6,
  output s7
);

  wire and_1_out, and_2_out, and_3_out, and_4_out, and_5_out, and_6_out, and_7_out, and_8_out, and_9_out,
       and_10_out, and_11_out, and_12_out, and_13_out, and_14_out, and_15_out, and_16_out, and_17_out,
       and_18_out, and_19_out, and_20_out, and_21_out, and_22_out, and_23_out, and_24_out, and_25_out,
       and_26_out, and_27_out, and_28_out, and_29_out, and_30_out, and_31_out, not_1_out, not_2_out,
       not_3_out, not_4_out;

  not not_1 (not_1_out, b);
  not not_2 (not_2_out, c);
  not not_3 (not_3_out, d);
  not not_4 (not_4_out, e);
  and and_1 (and_1_out, b, not_3_out, e);
  and and_2 (and_2_out, not_1_out, not_3_out, not_4_out);
  and and_3 (and_3_out, not_1_out, d, e);
  and and_4 (and_4_out, not_2_out, not_3_out);
  and and_5 (and_5_out, b, not_2_out);
  and and_6 (and_6_out, c, d, not_4_out);
  and and_7 (and_7_out, not_1_out, not_2_out, not_3_out);
  and and_8 (and_8_out, not_1_out, c, d);
  and and_9 (and_9_out, b, not_2_out, d);
  and and_10 (and_10_out, b, not_3_out, not_4_out);
  and and_11 (and_11_out, not_2_out, not_4_out);
  and and_12 (and_12_out, not_1_out, d);
  and and_13 (and_13_out, b, not_3_out);
  and and_14 (and_14_out, not_1_out, d);
  and and_15 (and_15_out, b, not_3_out);
  and and_16 (and_16_out, b, c, not_3_out, e);
  and and_17 (and_17_out, not_1_out, not_2_out, e);
  and and_18 (and_18_out, not_1_out, not_3_out, not_4_out);
  and and_19 (and_19_out, not_1_out, c, d);
  and and_20 (and_20_out, b, not_2_out, not_4_out);
  and and_21 (and_21_out, b, not_2_out, d);
  and and_22 (and_22_out, b, d, not_4_out);
  and and_23 (and_23_out, not_1_out, not_3_out, not_4_out);
  and and_24 (and_24_out, b, not_2_out, not_4_out);
  and and_25 (and_25_out, c, d, not_4_out);
  and and_26 (and_26_out, not_1_out, not_2_out);
  and and_27 (and_27_out, not_3_out, not_4_out);
  and and_28 (and_28_out, not_1_out, d, e);
  and and_29 (and_29_out, not_2_out, d);
  and and_30 (and_30_out, b, c, not_3_out);
  and and_31 (and_31_out, b, not_4_out);
  or or_1 (s1, and_1_out, and_2_out, and_3_out, and_4_out, and_5_out, and_6_out);
  or or_2 (s2, and_7_out, and_8_out, and_9_out, and_10_out, and_11_out);
  or or_3 (s3, and_12_out, c, and_13_out);
  or or_4 (s4, not_2_out, e, and_14_out, and_15_out);
  or or_5 (s5, and_16_out, and_17_out, and_18_out, and_19_out, and_20_out, and_21_out, and_22_out);
  or or_6 (s6, and_23_out, and_24_out, and_25_out);
  or or_7 (s7, and_26_out, and_27_out, and_28_out, and_29_out, and_30_out, and_31_out);
endmodule

module SEGMENT0_1 (
  input  a,
  input  b,
  input  c,
  input  d,
  input  e,
  output s1,
  output s2,
  output s3,
  output s4,
  output s5,
  output s6,
  output s7
);

  wire and_1_out, and_2_out, and_3_out, and_4_out, and_5_out, and_6_out, and_7_out, and_8_out, not_1_out,
       not_2_out, not_3_out, not_4_out;

  not not_1 (not_1_out, a);
  not not_2 (not_2_out, c);
  not not_3 (not_3_out, d);
  not not_4 (not_4_out, e);
  and and_1 (and_1_out, not_1_out, c, d, e);
  and and_2 (and_2_out, a, not_2_out, not_3_out, not_4_out);
  and and_3 (and_3_out, a, not_2_out, not_3_out, not_4_out);
  and and_4 (and_4_out, not_1_out, c, d, e);
  and and_5 (and_5_out, a, not_2_out, not_3_out, not_4_out);
  and and_6 (and_6_out, not_1_out, c, d, e);
  and and_7 (and_7_out, a, not_2_out, not_3_out, not_4_out);
  and and_8 (and_8_out, not_1_out, c, d, e);
  or or_1 (s1, and_1_out, b, and_2_out);
  or or_2 (s2, and_3_out, and_4_out, b);
  or or_3 (s5, and_5_out, and_6_out, b);
  or or_4 (s6, and_7_out, and_8_out, b);

  assign s3 = 1'b1;
  assign s4 = 1'b1;
  assign s7 = 1'b0;
endmodule

module HANDL_IT (
  input  a,
  input  b,
  input  c,
  input  d,
  input  e,
  output x,
  output y,
  output z
);

  wire and_1_out, and_2_out, not_1_out, not_2_out, not_3_out;

  not not_1 (not_1_out, a);
  not not_2 (not_2_out, b);
  not not_3 (not_3_out, c);
  and and_1 (and_1_out, not_1_out, not_2_out);
  and and_2 (and_2_out, not_1_out, not_3_out);
  and and_3 (y, not_1_out, b, c);
  or or_1 (x, and_1_out, and_2_out);

  assign z = a;
endmodule
