// Logisim project Magic_8_Ball.circ as structural Verilog: 2 circuits, main circuit main
module Magic8Ball (
  input  rst,
  output [6:0] ttyOut,
  output ttyClk,
  output ttyClr
);

  wire CONTER_carry, ena, not_1_out, or_1_out;
  wire [4:0] random_1_out;
  wire [7:7] ROMY_data;
  wire [11:0] CONTER_q, multiplexer_1_out;

  Multiplexer #(.select(5), .width(12)) multiplexer_1 (
    .in0(12'h1), .in1(12'hf), .in2(12'h22), .in3(12'h32), .in4(12'h41), .in5(12'h54), .in6(12'h64),
    .in7(12'h70), .in8(12'h7d), .in9(12'h81), .in10(12'h94), .in11(12'ha9), .in12(12'hb8), .in13(12'hd1),
    .in14(12'he4), .in15(12'hfe), .in16(12'h111), .in17(12'h120), .in18(12'h132), .in19(12'h146),
    .in20(12'h1), .in21(12'hf), .in22(12'h22), .in23(12'h32), .in24(12'h41), .in25(12'h54), .in26(12'h64),
    .in27(12'h70), .in28(12'h7d), .in29(12'h81), .in30(12'h94), .in31(12'ha9), .out(multiplexer_1_out),
    .sel(random_1_out));
  Random #(.width(5)) random_1 (.clk(ttyClr), .out(random_1_out));  // open: clr, next
  or or_1 (or_1_out, ttyClk, ttyClr);
  Counter #(.max('hfff), .width(12)) CONTER (
    .load(ttyClr), .count(ena), .clk(or_1_out), .D(multiplexer_1_out), .carry(CONTER_carry), .Q(CONTER_q));  // open: clr, up
  ROM #(.addrWidth(12)) ROMY (.addr(CONTER_q), .data({ROMY_data[7], ttyOut}));
  not not_1 (not_1_out, ena);
  and and_1 (ttyClr, rst, not_1_out);
  BitFinder #(.width(7)) bitfinder_1 (.in(ttyOut), .found(ena));  // open: index
  Clock #(.lowDuration(5)) clock_1 (.out(ttyClk));

  // Other names for the same wires on the sheet: ctrclk = ttyClk; load = ttyClr; rngclk = ttyClr

  // Notes on the sheet:
  //   contents of ROMY (hex, n*v repeats v):
  //   0 49 74 20 69 73 20 63 65 72 74 61 69 6e 0 49 74 20 69 73 20 64 65 63 69 64 65 64 6c 79 20 73 6f 0
  //   57 69 74 68 6f 75 74 20 61 20 64 6f 75 62 74 0 59 65 73 20 64 65 66 69 6e 69 74 65 6c 79 0 59 6f 75
  //   20 6d 61 79 20 72 65 6c 79 20 6f 6e 20 69 74 0 41 73 20 49 20 73 65 65 20 69 74 20 79 65 73 0 4d 6f
  //   73 74 20 6c 69 6b 65 6c 79 0 4f 75 74 6c 6f 6f 6b 20 67 6f 6f 64 0 59 65 73 0 53 69 67 6e 73 20 70
  //   6f 69 6e 74 20 74 6f 20 79 65 73 0 52 65 70 6c 79 20 68 61 7a 79 20 74 72 79 20 61 67 61 69 6e 0 41
  //   73 6b 20 61 67 61 69 6e 20 6c 61 74 65 72 0 42 65 74 74 65 72 20 6e 6f 74 20 74 65 6c 6c 20 79 6f 75
  //   20 6e 6f 77 0 43 61 6e 6e 6f 74 20 70 72 65 64 69 63 74 20 6e 6f 77 0 43 6f 6e 63 65 6e 74 72 61 74
  //   65 20 61 6e 64 20 61 73 6b 20 61 67 61 69 6e 0 44 6f 20 6e 6f 74 20 63 6f 75 6e 74 20 6f 6e 20 69 74
  //   0 4d 79 20 72 65 70 6c 79 20 69 73 20 6e 6f 0 4d 79 20 73 6f 75 72 63 65 73 20 73 61 79 20 6e 6f 0
  //   4f 75 74 6c 6f 6f 6b 20 6e 6f 74 20 73 6f 20 67 6f 6f 64 0 56 65 72 79 20 64 6f 75 62 74 66 75 6c
endmodule

module main (
);

  wire Ask_out, magic8ball_1_ttyclk, magic8ball_1_ttyclr;
  wire [6:0] magic8ball_1_ttyout;

  Button Ask (.out(Ask_out));
  Magic8Ball magic8ball_1 (
    .rst(Ask_out), .ttyOut(magic8ball_1_ttyout), .ttyClk(magic8ball_1_ttyclk), .ttyClr(magic8ball_1_ttyclr));
  TTY tty_1 (.data(magic8ball_1_ttyout), .clk(magic8ball_1_ttyclk), .clr(magic8ball_1_ttyclr));  // open: we
endmodule
