// Logisim project RAM_TEST_.circ as structural Verilog
module RAM_TEST (
);

  wire abl, clk, clr_out, ena, mode, rd, rst_out, wrt;
  wire [6:0] into;
  wire [7:0] counter_1_q, ram_1_dout;

  Counter counter_1 (.clr(rst_out), .clk(clk), .Q(counter_1_q));  // open: load, up, count, D, carry
  Button rst (.out(rst_out));
  Button clock (.out(clk));
  Button rd_wrt (.out(mode));
  and and_1 (ena, wrt, clk);
  T_Flip_Flop t_ff_1 (.T(1'b1), .clk(mode), .Q(wrt), .Qn(rd));  // open: reset, preset
  and and_2 (abl, rd, clk);
  LED led_1 (.in(wrt));
  Keyboard #(.buflen(80)) keyboard_1 (.clk(ena), .data(into));  // open: re, clr, avail
  RAM ram_1 (.addr(counter_1_q), .we(wrt), .oe(rd), .clk(clk), .din({1'b0, into}), .dout(ram_1_dout));
  LED led_2 (.in(rd));
  TTY #(.cols(45), .rows(13)) tty_1 (.data(ram_1_dout[6:0]), .clk(abl), .clr(clr_out));  // open: we
  Button clr (.out(clr_out));
endmodule
