// Logisim project RegisterFILE.circ as structural Verilog: 5 circuits, main circuit main
module main (
  input  WriteSignal,
  input  [4:0] reg1,
  input  [4:0] reg2,
  input  [4:0] regWrite,
  input  [31:0] Data,
  output [31:0] out_6,
  output [31:0] out_7
);

  fileregister fileregister_1 (
    .WriteSignl(WriteSignal), .registre1(reg1), .registre2(reg2), .regWrite(regWrite), .DataWrite(Data),
    .data1(out_6), .data2(out_7));

  // Notes on the sheet:
  //     1- set the signal to one
  //   Best Regrads.
  //   These circuite will help in designg the risc-v architecture
  //   NB: if you want to Write then you should follow :
  //    2 - reset it to 0 before any other operation
  //   These circuite is build by Student.Ahmed Fouatih Hamza FAIZ ,         ARCHI 2   winter-2025
endmodule

module Dlatch (
  input  C,
  input  D,
  output Q,
  output Qbar
);

  wire and_1_out, and_2_out, not_1_out;

  and and_1 (and_1_out, C, not_1_out);
  not not_1 (not_1_out, D);
  and and_2 (and_2_out, C, D);
  nor nor_1 (Q, and_1_out, Qbar);
  nor nor_2 (Qbar, Q, and_2_out);
endmodule

module Dflipflop (
  input  C,
  input  D,
  output Q,
  output Qbar
);

  wire dlatch_1_q, not_1_out;

  not not_1 (not_1_out, C);
  Dlatch dlatch_1 (.C(C), .D(D), .Q(dlatch_1_q));  // open: Qbar
  Dlatch dlatch_2 (.C(not_1_out), .D(dlatch_1_q), .Q(Q), .Qbar(Qbar));
endmodule

module regster (
  input  C,
  input  [31:0] D,
  output [31:0] Q
);

  Dflipflop dflipflop_1 (.C(C), .D(D[0]), .Q(Q[0]));  // open: Qbar
  Dflipflop dflipflop_2 (.C(C), .D(D[1]), .Q(Q[1]));  // open: Qbar
  Dflipflop dflipflop_3 (.C(C), .D(D[2]), .Q(Q[2]));  // open: Qbar
  Dflipflop dflipflop_4 (.C(C), .D(D[3]), .Q(Q[3]));  // open: Qbar
  Dflipflop dflipflop_5 (.C(C), .D(D[4]), .Q(Q[4]));  // open: Qbar
  Dflipflop dflipflop_6 (.C(C), .D(D[5]), .Q(Q[5]));  // open: Qbar
  Dflipflop dflipflop_7 (.C(C), .D(D[6]), .Q(Q[6]));  // open: Qbar
  Dflipflop dflipflop_8 (.C(C), .D(D[7]), .Q(Q[7]));  // open: Qbar
  Dflipflop dflipflop_9 (.C(C), .D(D[8]), .Q(Q[8]));  // open: Qbar
  Dflipflop dflipflop_10 (.C(C), .D(D[9]), .Q(Q[9]));  // open: Qbar
  Dflipflop dflipflop_11 (.C(C), .D(D[10]), .Q(Q[10]));  // open: Qbar
  Dflipflop dflipflop_12 (.C(C), .D(D[11]), .Q(Q[11]));  // open: Qbar
  Dflipflop dflipflop_13 (.C(C), .D(D[12]), .Q(Q[12]));  // open: Qbar
  Dflipflop dflipflop_14 (.C(C), .D(D[13]), .Q(Q[13]));  // open: Qbar
  Dflipflop dflipflop_15 (.C(C), .D(D[14]), .Q(Q[14]));  // open: Qbar
  Dflipflop dflipflop_16 (.C(C), .D(D[15]), .Q(Q[15]));  // open: Qbar
  Dflipflop dflipflop_17 (.C(C), .D(D[16]), .Q(Q[16]));  // open: Qbar
  Dflipflop dflipflop_18 (.C(C), .D(D[17]), .Q(Q[17]));  // open: Qbar
  Dflipflop dflipflop_19 (.C(C), .D(D[18]), .Q(Q[18]));  // open: Qbar
  Dflipflop dflipflop_20 (.C(C), .D(D[19]), .Q(Q[19]));  // open: Qbar
  Dflipflop dflipflop_21 (.C(C), .D(D[20]), .Q(Q[20]));  // open: Qbar
  Dflipflop dflipflop_22 (.C(C), .D(D[21]), .Q(Q[21]));  // open: Qbar
  Dflipflop dflipflop_23 (.C(C), .D(D[22]), .Q(Q[22]));  // open: Qbar
  Dflipflop dflipflop_24 (.C(C), .D(D[23]), .Q(Q[23]));  // open: Qbar
  Dflipflop dflipflop_25 (.C(C), .D(D[24]), .Q(Q[24]));  // open: Qbar
  Dflipflop dflipflop_26 (.C(C), .D(D[25]), .Q(Q[25]));  // open: Qbar
  Dflipflop dflipflop_27 (.C(C), .D(D[26]), .Q(Q[26]));  // open: Qbar
  Dflipflop dflipflop_28 (.C(C), .D(D[27]), .Q(Q[27]));  // open: Qbar
  Dflipflop dflipflop_29 (.C(C), .D(D[28]), .Q(Q[28]));  // open: Qbar
  Dflipflop dflipflop_30 (.C(C), .D(D[29]), .Q(Q[29]));  // open: Qbar
  Dflipflop dflipflop_31 (.C(C), .D(D[30]), .Q(Q[30]));  // open: Qbar
  Dflipflop dflipflop_32 (.C(C), .D(D[31]), .Q(Q[31]));  // open: Qbar
endmodule

module fileregister (
  input  WriteSignl,
  input  [4:0] registre1,
  input  [4:0] registre2,
  input  [4:0] regWrite,
  input  [31:0] DataWrite,
  output [31:0] data1,
  output [31:0] data2
);

  wire and_1_out, and_2_out, and_3_out, and_4_out, and_5_out, and_6_out, and_7_out, and_8_out, and_9_out,
       and_10_out, and_11_out, and_12_out, and_13_out, and_14_out, and_15_out, and_16_out, and_17_out,
       and_18_out, and_19_out, and_20_out, and_21_out, and_22_out, and_23_out, and_24_out, and_25_out,
       and_26_out, and_27_out, and_28_out, and_29_out, and_30_out, and_31_out, and_32_out, decoder_1_out0,
       decoder_1_out1, decoder_1_out2, decoder_1_out3, decoder_1_out4, decoder_1_out5, decoder_1_out6,
       decoder_1_out7, decoder_1_out8, decoder_1_out9, decoder_1_out10, decoder_1_out11, decoder_1_out12,
       decoder_1_out13, decoder_1_out14, decoder_1_out15, decoder_1_out16, decoder_1_out17, decoder_1_out18,
       decoder_1_out19, decoder_1_out20, decoder_1_out21, decoder_1_out22, decoder_1_out23, decoder_1_out24,
       decoder_1_out25, decoder_1_out26, decoder_1_out27, decoder_1_out28, decoder_1_out29, decoder_1_out30,
       decoder_1_out31;
  wire [31:0] regster_1_q, regster_2_q, regster_3_q, regster_4_q, regster_5_q, regster_6_q, regster_7_q,
       regster_8_q, regster_9_q, regster_10_q, regster_11_q, regster_12_q, regster_13_q, regster_14_q,
       regster_15_q, regster_16_q, regster_17_q, regster_18_q, regster_19_q, regster_20_q, regster_21_q,
       regster_22_q, regster_23_q, regster_24_q, regster_25_q, regster_26_q, regster_27_q, regster_28_q,
       regster_29_q, regster_30_q, regster_31_q, regster_32_q;

  Decoder #(.select(5)) decoder_1 (
    .out0(decoder_1_out0), .out1(decoder_1_out1), .out2(decoder_1_out2), .out3(decoder_1_out3),
    .out4(decoder_1_out4), .out5(decoder_1_out5), .out6(decoder_1_out6), .out7(decoder_1_out7),
    .out8(decoder_1_out8), .out9(decoder_1_out9), .out10(decoder_1_out10), .out11(decoder_1_out11),
    .out12(decoder_1_out12), .out13(decoder_1_out13), .out14(decoder_1_out14), .out15(decoder_1_out15),
    .out16(decoder_1_out16), .out17(decoder_1_out17), .out18(decoder_1_out18), .out19(decoder_1_out19),
    .out20(decoder_1_out20), .out21(decoder_1_out21), .out22(decoder_1_out22), .out23(decoder_1_out23),
    .out24(decoder_1_out24), .out25(decoder_1_out25), .out26(decoder_1_out26), .out27(decoder_1_out27),
    .out28(decoder_1_out28), .out29(decoder_1_out29), .out30(decoder_1_out30), .out31(decoder_1_out31),
    .sel(regWrite));  // open: en
  and and_1 (and_1_out, WriteSignl, decoder_1_out0);
  and and_2 (and_2_out, WriteSignl, decoder_1_out1);
  and and_3 (and_3_out, WriteSignl, decoder_1_out2);
  and and_4 (and_4_out, WriteSignl, decoder_1_out3);
  and and_5 (and_5_out, WriteSignl, decoder_1_out4);
  and and_6 (and_6_out, WriteSignl, decoder_1_out5);
  and and_7 (and_7_out, WriteSignl, decoder_1_out6);
  and and_8 (and_8_out, WriteSignl, decoder_1_out7);
  and and_9 (and_9_out, WriteSignl, decoder_1_out8);
  and and_10 (and_10_out, WriteSignl, decoder_1_out9);
  and and_11 (and_11_out, WriteSignl, decoder_1_out10);
  and and_12 (and_12_out, WriteSignl, decoder_1_out11);
  and and_13 (and_13_out, WriteSignl, decoder_1_out12);
  and and_14 (and_14_out, WriteSignl, decoder_1_out13);
  and and_15 (and_15_out, WriteSignl, decoder_1_out14);
  and and_16 (and_16_out, WriteSignl, decoder_1_out15);
  and and_17 (and_17_out, WriteSignl, decoder_1_out16);
  and and_18 (and_18_out, WriteSignl, decoder_1_out17);
  and and_19 (and_19_out, WriteSignl, decoder_1_out18);
  and and_20 (and_20_out, WriteSignl, decoder_1_out19);
  and and_21 (and_21_out, WriteSignl, decoder_1_out20);
  and and_22 (and_22_out, WriteSignl, decoder_1_out21);
  and and_23 (and_23_out, WriteSignl, decoder_1_out22);
  and and_24 (and_24_out, WriteSignl, decoder_1_out23);
  and and_25 (and_25_out, WriteSignl, decoder_1_out24);
  and and_26 (and_26_out, WriteSignl, decoder_1_out25);
  and and_27 (and_27_out, WriteSignl, decoder_1_out26);
  and and_28 (and_28_out, WriteSignl, decoder_1_out27);
  and and_29 (and_29_out, WriteSignl, decoder_1_out28);
  and and_30 (and_30_out, WriteSignl, decoder_1_out29);
  and and_31 (and_31_out, WriteSignl, decoder_1_out30);
  and and_32 (and_32_out, WriteSignl, decoder_1_out31);
  regster regster_1 (.C(and_1_out), .D(DataWrite), .Q(regster_1_q));
  regster regster_2 (.C(and_2_out), .D(DataWrite), .Q(regster_2_q));
  regster regster_3 (.C(and_3_out), .D(DataWrite), .Q(regster_3_q));
  regster regster_4 (.C(and_4_out), .D(DataWrite), .Q(regster_4_q));
  regster regster_5 (.C(and_5_out), .D(DataWrite), .Q(regster_5_q));
  regster regster_6 (.C(and_6_out), .D(DataWrite), .Q(regster_6_q));
  regster regster_7 (.C(and_7_out), .D(DataWrite), .Q(regster_7_q));
  regster regster_8 (.C(and_8_out), .D(DataWrite), .Q(regster_8_q));
  regster regster_9 (.C(and_9_out), .D(DataWrite), .Q(regster_9_q));
  regster regster_10 (.C(and_10_out), .D(DataWrite), .Q(regster_10_q));
  regster regster_11 (.C(and_11_out), .D(DataWrite), .Q(regster_11_q));
  regster regster_12 (.C(and_12_out), .D(DataWrite), .Q(regster_12_q));
  regster regster_13 (.C(and_13_out), .D(DataWrite), .Q(regster_13_q));
  regster regster_14 (.C(and_14_out), .D(DataWrite), .Q(regster_14_q));
  regster regster_15 (.C(and_15_out), .D(DataWrite), .Q(regster_15_q));
  regster regster_16 (.C(and_16_out), .D(DataWrite), .Q(regster_16_q));
  regster regster_17 (.C(and_17_out), .D(DataWrite), .Q(regster_17_q));
  regster regster_18 (.C(and_18_out), .D(DataWrite), .Q(regster_18_q));
  regster regster_19 (.C(and_19_out), .D(DataWrite), .Q(regster_19_q));
  regster regster_20 (.C(and_20_out), .D(DataWrite), .Q(regster_20_q));
  regster regster_21 (.C(and_21_out), .D(DataWrite), .Q(regster_21_q));
  regster regster_22 (.C(and_22_out), .D(DataWrite), .Q(regster_22_q));
  regster regster_23 (.C(and_23_out), .D(DataWrite), .Q(regster_23_q));
  regster regster_24 (.C(and_24_out), .D(DataWrite), .Q(regster_24_q));
  regster regster_25 (.C(and_25_out), .D(DataWrite), .Q(regster_25_q));
  regster regster_26 (.C(and_26_out), .D(DataWrite), .Q(regster_26_q));
  regster regster_27 (.C(and_27_out), .D(DataWrite), .Q(regster_27_q));
  regster regster_28 (.C(and_28_out), .D(DataWrite), .Q(regster_28_q));
  regster regster_29 (.C(and_29_out), .D(DataWrite), .Q(regster_29_q));
  regster regster_30 (.C(and_30_out), .D(DataWrite), .Q(regster_30_q));
  regster regster_31 (.C(and_31_out), .D(DataWrite), .Q(regster_31_q));
  regster regster_32 (.C(and_32_out), .D(DataWrite), .Q(regster_32_q));
  Multiplexer #(.select(5), .width(32)) multiplexer_1 (
    .in0(regster_1_q), .in1(regster_2_q), .in2(regster_3_q), .in3(regster_4_q), .in4(regster_5_q),
    .in5(regster_6_q), .in6(regster_7_q), .in7(regster_8_q), .in8(regster_9_q), .in9(regster_10_q),
    .in10(regster_11_q), .in11(regster_12_q), .in12(regster_13_q), .in13(regster_14_q), .in14(regster_15_q),
    .in15(regster_16_q), .in16(regster_17_q), .in17(regster_18_q), .in18(regster_19_q), .in19(regster_20_q),
    .in20(regster_21_q), .in21(regster_22_q), .in22(regster_23_q), .in23(regster_24_q), .in24(regster_25_q),
    .in25(regster_26_q), .in26(regster_27_q), .in27(regster_28_q), .in28(regster_29_q), .in29(regster_30_q),
    .in30(regster_31_q), .in31(regster_32_q), .out(data1), .sel(registre1));
  Multiplexer #(.select(5), .width(32)) multiplexer_2 (
    .in0(regster_1_q), .in1(regster_2_q), .in2(regster_3_q), .in3(regster_4_q), .in4(regster_5_q),
    .in5(regster_6_q), .in6(regster_7_q), .in7(regster_8_q), .in8(regster_9_q), .in9(regster_10_q),
    .in10(regster_11_q), .in11(regster_12_q), .in12(regster_13_q), .in13(regster_14_q), .in14(regster_15_q),
    .in15(regster_16_q), .in16(regster_17_q), .in17(regster_18_q), .in18(regster_19_q), .in19(regster_20_q),
    .in20(regster_21_q), .in21(regster_22_q), .in22(regster_23_q), .in23(regster_24_q), .in24(regster_25_q),
    .in25(regster_26_q), .in26(regster_27_q), .in27(regster_28_q), .in28(regster_29_q), .in29(regster_30_q),
    .in30(regster_31_q), .in31(regster_32_q), .out(data2), .sel(registre2));
endmodule
